# Fritzing sketch Circuito (saved by Fritzing 0.9.3b)
breadboards: 1

parts:
  R1 = Photocell (LDR) [package=THT]
  Componente1 = Arduino Uno (Rev3)
  Componente2 = Bluetooth HC-06
  Componente3 = Soil Moisture Sensor
  Power_plug1 = Power plug
  VCC1 = Battery block 9V
  M1 = DC Motor
  LED1 = LED - 5mm [color="Red (633nm)" package="5 mm [THT]"]
  LED2 = LED - 5mm [color="Red (633nm)" package="5 mm [THT]"]  # not connected
  LED3 = LED - 5mm [color="Red (633nm)" package="5 mm [THT]"]
  R2 = Resistor [tolerance=±5% resistance=220 package=THT]

nets:
  N1: R1.pin_0, Componente1.A0, R2.Pin_1
  VCC: R1.pin_1, Componente1.5V, Componente2.VCC, Componente3.VCC
  N2: Componente1.A1, Componente3.SIG
  N3: Componente1.D0/RX, Componente2.TXD
  N4: Componente1.D1/TX, Componente2.RXD
  N5: Componente1.D2, M1.pin_2
  N6: Componente1.D3_PWM, LED3.anode
  GND: Componente1.GND, Componente2.GND, Componente3.GND, M1.pin_1, LED1.cathode, R2.Pin_0
  N7: Power_plug1.VCC, VCC1.-
  N8: Power_plug1.GND, VCC1.+

// code stored in the sketch: Invernadero_inteligente.ino
/*Invernadero inteligente */

void setup() {
  // put your setup code here, to run once:

}

void loop() {
  // put your main code here, to run repeatedly:

}
